// Logisim project Tv-tennis.circ as structural Verilog: 4 circuits, main circuit main
module main (
  input  [31:0] bus_0
);

  Hex_Digit_Display hex_digit_display_1 ();  // open: value, dp
  Hex_Digit_Display hex_digit_display_2 ();  // open: value, dp
  Joystick #(.bits(5)) joystick_1 ();  // open: x, y
  Button button_1 ();  // open: out
  DotMatrix #(.matrixcols(32), .matrixrows(32)) dotmatrix_1 (
    .col0(bus_0), .col1(bus_0), .col2(bus_0), .col3(bus_0), .col4(bus_0), .col5(bus_0), .col6(bus_0),
    .col7(bus_0), .col8(bus_0), .col9(bus_0), .col10(bus_0), .col11(bus_0), .col12(bus_0), .col13(bus_0),
    .col14(bus_0), .col15(bus_0), .col16(bus_0), .col17(bus_0), .col18(bus_0), .col19(bus_0), .col20(bus_0),
    .col21(bus_0), .col22(bus_0), .col23(bus_0), .col24(bus_0), .col25(bus_0), .col26(bus_0), .col27(bus_0),
    .col28(bus_0), .col29(bus_0), .col30(bus_0), .col31(bus_0));
  Hex_Digit_Display hex_digit_display_3 ();  // open: value, dp
  Hex_Digit_Display hex_digit_display_4 ();  // open: value, dp
endmodule

module video_subsystem (
  input  [4:0] chipID,
  input  [4:0] ballX,
  input  [4:0] ballY,
  input  [4:0] leftbatY,
  input  [4:0] rightbatX
);
endmodule

module videochip (
  input  [4:0] chipID,
  input  [4:0] ballX,
  input  [4:0] ballY,
  input  [4:0] leftbatY,
  input  [4:0] rightbatX,
  output [31:0] video_column,
  output [4:0] chipID_2,
  output [4:0] ballX_2,
  output [4:0] ballY_2,
  output [4:0] leftbatY_2,
  output [4:0] rightbatX_2
);

  wire [31:0] decoder_1_out0;

  Decoder #(.select(5)) decoder_1 (
    .out0(decoder_1_out0[0]), .out1(decoder_1_out0[1]), .out2(decoder_1_out0[2]), .out3(decoder_1_out0[3]),
    .out4(decoder_1_out0[4]), .out5(decoder_1_out0[5]), .out6(decoder_1_out0[6]), .out7(decoder_1_out0[7]),
    .out8(decoder_1_out0[8]), .out9(decoder_1_out0[9]), .out10(decoder_1_out0[10]),
    .out11(decoder_1_out0[11]), .out12(decoder_1_out0[12]), .out13(decoder_1_out0[13]),
    .out14(decoder_1_out0[14]), .out15(decoder_1_out0[15]), .out16(decoder_1_out0[16]),
    .out17(decoder_1_out0[17]), .out18(decoder_1_out0[18]), .out19(decoder_1_out0[19]),
    .out20(decoder_1_out0[20]), .out21(decoder_1_out0[21]), .out22(decoder_1_out0[22]),
    .out23(decoder_1_out0[23]), .out24(decoder_1_out0[24]), .out25(decoder_1_out0[25]),
    .out26(decoder_1_out0[26]), .out27(decoder_1_out0[27]), .out28(decoder_1_out0[28]),
    .out29(decoder_1_out0[29]), .out30(decoder_1_out0[30]), .out31(decoder_1_out0[31]));  // open: sel, en
  inc inc_1 (.in_1(chipID), .out_2(chipID_2));
endmodule

module inc (
  input  [4:0] in_1,
  output [4:0] out_2
);

  wire [4:1] and_1_out;
  wire [4:4] and_1_out_2;

  assign out_2 = in_1 ^ {and_1_out, 1'b1};  // XOR_Gate xor_1, 5 bits wide
  assign {and_1_out_2[4], and_1_out} = {and_1_out, 1'b1} & in_1;  // AND_Gate and_1, 5 bits wide
endmodule
