// Logisim project Tv-tennis ().circ as structural Verilog
module main (
);

  wire clock_1_out, R_out;
  wire [4:0] controller_1_p9, controller_1_p10, controller_1_p11, controller_1_p12, controller_1_p13,
       video_subsystem_1_ballx_2, video_subsystem_1_bally_2, video_subsystem_1_chipid_2,
       video_subsystem_1_leftbaty_2, video_subsystem_1_rightbatx_2, video_subsystem_2_ballx_2,
       video_subsystem_2_bally_2, video_subsystem_2_chipid_2, video_subsystem_2_leftbaty_2,
       video_subsystem_2_rightbatx_2, video_subsystem_3_ballx_2, video_subsystem_3_bally_2,
       video_subsystem_3_chipid_2, video_subsystem_3_leftbaty_2, video_subsystem_3_rightbatx_2;
  wire [7:0] A, B, Vxy;
  wire [31:0] video_subsystem_1_videocolumn, video_subsystem_1_videocolumn_2,
       video_subsystem_1_videocolumn_3, video_subsystem_1_videocolumn_4, video_subsystem_1_videocolumn_5,
       video_subsystem_1_videocolumn_6, video_subsystem_1_videocolumn_7, video_subsystem_1_videocolumn_8,
       video_subsystem_2_videocolumn, video_subsystem_2_videocolumn_2, video_subsystem_2_videocolumn_3,
       video_subsystem_2_videocolumn_4, video_subsystem_2_videocolumn_5, video_subsystem_2_videocolumn_6,
       video_subsystem_2_videocolumn_7, video_subsystem_2_videocolumn_8, video_subsystem_3_videocolumn,
       video_subsystem_3_videocolumn_2, video_subsystem_3_videocolumn_3, video_subsystem_3_videocolumn_4,
       video_subsystem_3_videocolumn_5, video_subsystem_3_videocolumn_6, video_subsystem_3_videocolumn_7,
       video_subsystem_3_videocolumn_8, video_subsystem_4_videocolumn, video_subsystem_4_videocolumn_2,
       video_subsystem_4_videocolumn_3, video_subsystem_4_videocolumn_4, video_subsystem_4_videocolumn_5,
       video_subsystem_4_videocolumn_6, video_subsystem_4_videocolumn_7, video_subsystem_4_videocolumn_8;

  Button R (.out(R_out));
  Clock clock_1 (.out(clock_1_out));
  Hex_Digit_Display hex_digit_display_1 ();  // open: value, dp
  Hex_Digit_Display hex_digit_display_2 ();  // open: value, dp
  Joystick #(.bits(5)) joystick_1 ();  // open: x, y
  DotMatrix #(.matrixcols(32), .matrixrows(32)) dotmatrix_1 (
    .col0(video_subsystem_1_videocolumn), .col1(video_subsystem_1_videocolumn_2),
    .col2(video_subsystem_1_videocolumn_3), .col3(video_subsystem_1_videocolumn_4),
    .col4(video_subsystem_1_videocolumn_5), .col5(video_subsystem_1_videocolumn_6),
    .col6(video_subsystem_1_videocolumn_7), .col7(video_subsystem_1_videocolumn_8),
    .col8(video_subsystem_2_videocolumn), .col9(video_subsystem_2_videocolumn_2),
    .col10(video_subsystem_2_videocolumn_3), .col11(video_subsystem_2_videocolumn_4),
    .col12(video_subsystem_2_videocolumn_5), .col13(video_subsystem_2_videocolumn_6),
    .col14(video_subsystem_2_videocolumn_7), .col15(video_subsystem_2_videocolumn_8),
    .col16(video_subsystem_3_videocolumn), .col17(video_subsystem_3_videocolumn_2),
    .col18(video_subsystem_3_videocolumn_3), .col19(video_subsystem_3_videocolumn_4),
    .col20(video_subsystem_3_videocolumn_5), .col21(video_subsystem_3_videocolumn_6),
    .col22(video_subsystem_3_videocolumn_7), .col23(video_subsystem_3_videocolumn_8),
    .col24(video_subsystem_4_videocolumn), .col25(video_subsystem_4_videocolumn_2),
    .col26(video_subsystem_4_videocolumn_3), .col27(video_subsystem_4_videocolumn_4),
    .col28(video_subsystem_4_videocolumn_5), .col29(video_subsystem_4_videocolumn_6),
    .col30(video_subsystem_4_videocolumn_7), .col31(video_subsystem_4_videocolumn_8));
  // controller controller_1: pin names not known; wires that end beside it: Vxy, 5'b00101, 5'b00101, 5'b00101, 5'b00101, R_out, clock_1_out, A, controller_1_p9, controller_1_p10, controller_1_p11, controller_1_p12, controller_1_p13, B
  video_subsystem video_subsystem_1 (
    .chipID(controller_1_p9), .ballX(controller_1_p10), .ballY(controller_1_p11),
    .leftbatY(controller_1_p12), .rightbatX(controller_1_p13), .videocolumn(video_subsystem_1_videocolumn),
    .videocolumn_2(video_subsystem_1_videocolumn_2), .videocolumn_3(video_subsystem_1_videocolumn_3),
    .videocolumn_4(video_subsystem_1_videocolumn_4), .videocolumn_5(video_subsystem_1_videocolumn_5),
    .videocolumn_6(video_subsystem_1_videocolumn_6), .videocolumn_7(video_subsystem_1_videocolumn_7),
    .videocolumn_8(video_subsystem_1_videocolumn_8), .chipID_2(video_subsystem_1_chipid_2),
    .ballX_2(video_subsystem_1_ballx_2), .ballY_2(video_subsystem_1_bally_2),
    .leftbatY_2(video_subsystem_1_leftbaty_2), .rightbatX_2(video_subsystem_1_rightbatx_2));
  video_subsystem video_subsystem_2 (
    .chipID(video_subsystem_1_chipid_2), .ballX(video_subsystem_1_ballx_2),
    .ballY(video_subsystem_1_bally_2), .leftbatY(video_subsystem_1_leftbaty_2),
    .rightbatX(video_subsystem_1_rightbatx_2), .videocolumn(video_subsystem_2_videocolumn),
    .videocolumn_2(video_subsystem_2_videocolumn_2), .videocolumn_3(video_subsystem_2_videocolumn_3),
    .videocolumn_4(video_subsystem_2_videocolumn_4), .videocolumn_5(video_subsystem_2_videocolumn_5),
    .videocolumn_6(video_subsystem_2_videocolumn_6), .videocolumn_7(video_subsystem_2_videocolumn_7),
    .videocolumn_8(video_subsystem_2_videocolumn_8), .chipID_2(video_subsystem_2_chipid_2),
    .ballX_2(video_subsystem_2_ballx_2), .ballY_2(video_subsystem_2_bally_2),
    .leftbatY_2(video_subsystem_2_leftbaty_2), .rightbatX_2(video_subsystem_2_rightbatx_2));
  video_subsystem video_subsystem_3 (
    .chipID(video_subsystem_2_chipid_2), .ballX(video_subsystem_2_ballx_2),
    .ballY(video_subsystem_2_bally_2), .leftbatY(video_subsystem_2_leftbaty_2),
    .rightbatX(video_subsystem_2_rightbatx_2), .videocolumn(video_subsystem_3_videocolumn),
    .videocolumn_2(video_subsystem_3_videocolumn_2), .videocolumn_3(video_subsystem_3_videocolumn_3),
    .videocolumn_4(video_subsystem_3_videocolumn_4), .videocolumn_5(video_subsystem_3_videocolumn_5),
    .videocolumn_6(video_subsystem_3_videocolumn_6), .videocolumn_7(video_subsystem_3_videocolumn_7),
    .videocolumn_8(video_subsystem_3_videocolumn_8), .chipID_2(video_subsystem_3_chipid_2),
    .ballX_2(video_subsystem_3_ballx_2), .ballY_2(video_subsystem_3_bally_2),
    .leftbatY_2(video_subsystem_3_leftbaty_2), .rightbatX_2(video_subsystem_3_rightbatx_2));
  video_subsystem video_subsystem_4 (
    .chipID(video_subsystem_3_chipid_2), .ballX(video_subsystem_3_ballx_2),
    .ballY(video_subsystem_3_bally_2), .leftbatY(video_subsystem_3_leftbaty_2),
    .rightbatX(video_subsystem_3_rightbatx_2), .videocolumn(video_subsystem_4_videocolumn),
    .videocolumn_2(video_subsystem_4_videocolumn_2), .videocolumn_3(video_subsystem_4_videocolumn_3),
    .videocolumn_4(video_subsystem_4_videocolumn_4), .videocolumn_5(video_subsystem_4_videocolumn_5),
    .videocolumn_6(video_subsystem_4_videocolumn_6), .videocolumn_7(video_subsystem_4_videocolumn_7),
    .videocolumn_8(video_subsystem_4_videocolumn_8));  // open: chipID_2, ballX_2, ballY_2, leftbatY_2, rightbatX_2
  Hex_Digit_Display hex_digit_display_3 ();  // open: value, dp
  Hex_Digit_Display hex_digit_display_4 ();  // open: value, dp

  // Notes on the sheet:
  //   (тут надо разделить
  //   число на 2 цифры)
  //   score типа
endmodule

module video_subsystem (
  input  [4:0] chipID,
  input  [4:0] ballX,
  input  [4:0] ballY,
  input  [4:0] leftbatY,
  input  [4:0] rightbatX,
  output [31:0] videocolumn,
  output [31:0] videocolumn_2,
  output [31:0] videocolumn_3,
  output [31:0] videocolumn_4,
  output [31:0] videocolumn_5,
  output [31:0] videocolumn_6,
  output [31:0] videocolumn_7,
  output [31:0] videocolumn_8,
  output [4:0] chipID_2,
  output [4:0] ballX_2,
  output [4:0] ballY_2,
  output [4:0] leftbatY_2,
  output [4:0] rightbatX_2
);

  wire [4:0] videochip_1_ballx_2, videochip_1_bally_2, videochip_1_chipid_2, videochip_1_leftbaty_2,
       videochip_1_rightbatx_2, videochip_2_ballx_2, videochip_2_bally_2, videochip_2_chipid_2,
       videochip_2_leftbaty_2, videochip_2_rightbatx_2, videochip_3_ballx_2, videochip_3_bally_2,
       videochip_3_chipid_2, videochip_3_leftbaty_2, videochip_3_rightbatx_2, videochip_4_ballx_2,
       videochip_4_bally_2, videochip_4_chipid_2, videochip_4_leftbaty_2, videochip_4_rightbatx_2,
       videochip_5_ballx_2, videochip_5_bally_2, videochip_5_chipid_2, videochip_5_leftbaty_2,
       videochip_5_rightbatx_2, videochip_6_ballx_2, videochip_6_bally_2, videochip_6_chipid_2,
       videochip_6_leftbaty_2, videochip_6_rightbatx_2, videochip_7_ballx_2, videochip_7_bally_2,
       videochip_7_chipid_2, videochip_7_leftbaty_2, videochip_7_rightbatx_2;

  videochip videochip_1 (
    .chipID(chipID), .ballX(ballX), .ballY(ballY), .leftbatY(leftbatY), .rightbatX(rightbatX),
    .chipID_2(videochip_1_chipid_2), .ballX_2(videochip_1_ballx_2), .ballY_2(videochip_1_bally_2),
    .leftbatY_2(videochip_1_leftbaty_2), .rightbatX_2(videochip_1_rightbatx_2), .video_column(videocolumn));
  videochip videochip_2 (
    .chipID(videochip_1_chipid_2), .ballX(videochip_1_ballx_2), .ballY(videochip_1_bally_2),
    .leftbatY(videochip_1_leftbaty_2), .rightbatX(videochip_1_rightbatx_2), .chipID_2(videochip_2_chipid_2),
    .ballX_2(videochip_2_ballx_2), .ballY_2(videochip_2_bally_2), .leftbatY_2(videochip_2_leftbaty_2),
    .rightbatX_2(videochip_2_rightbatx_2), .video_column(videocolumn_2));
  videochip videochip_3 (
    .chipID(videochip_2_chipid_2), .ballX(videochip_2_ballx_2), .ballY(videochip_2_bally_2),
    .leftbatY(videochip_2_leftbaty_2), .rightbatX(videochip_2_rightbatx_2), .chipID_2(videochip_3_chipid_2),
    .ballX_2(videochip_3_ballx_2), .ballY_2(videochip_3_bally_2), .leftbatY_2(videochip_3_leftbaty_2),
    .rightbatX_2(videochip_3_rightbatx_2), .video_column(videocolumn_3));
  videochip videochip_4 (
    .chipID(videochip_3_chipid_2), .ballX(videochip_3_ballx_2), .ballY(videochip_3_bally_2),
    .leftbatY(videochip_3_leftbaty_2), .rightbatX(videochip_3_rightbatx_2), .chipID_2(videochip_4_chipid_2),
    .ballX_2(videochip_4_ballx_2), .ballY_2(videochip_4_bally_2), .leftbatY_2(videochip_4_leftbaty_2),
    .rightbatX_2(videochip_4_rightbatx_2), .video_column(videocolumn_4));
  videochip videochip_5 (
    .chipID(videochip_4_chipid_2), .ballX(videochip_4_ballx_2), .ballY(videochip_4_bally_2),
    .leftbatY(videochip_4_leftbaty_2), .rightbatX(videochip_4_rightbatx_2), .chipID_2(videochip_5_chipid_2),
    .ballX_2(videochip_5_ballx_2), .ballY_2(videochip_5_bally_2), .leftbatY_2(videochip_5_leftbaty_2),
    .rightbatX_2(videochip_5_rightbatx_2), .video_column(videocolumn_5));
  videochip videochip_6 (
    .chipID(videochip_5_chipid_2), .ballX(videochip_5_ballx_2), .ballY(videochip_5_bally_2),
    .leftbatY(videochip_5_leftbaty_2), .rightbatX(videochip_5_rightbatx_2), .chipID_2(videochip_6_chipid_2),
    .ballX_2(videochip_6_ballx_2), .ballY_2(videochip_6_bally_2), .leftbatY_2(videochip_6_leftbaty_2),
    .rightbatX_2(videochip_6_rightbatx_2), .video_column(videocolumn_6));
  videochip videochip_7 (
    .chipID(videochip_6_chipid_2), .ballX(videochip_6_ballx_2), .ballY(videochip_6_bally_2),
    .leftbatY(videochip_6_leftbaty_2), .rightbatX(videochip_6_rightbatx_2), .chipID_2(videochip_7_chipid_2),
    .ballX_2(videochip_7_ballx_2), .ballY_2(videochip_7_bally_2), .leftbatY_2(videochip_7_leftbaty_2),
    .rightbatX_2(videochip_7_rightbatx_2), .video_column(videocolumn_7));
  videochip videochip_8 (
    .chipID(videochip_7_chipid_2), .ballX(videochip_7_ballx_2), .ballY(videochip_7_bally_2),
    .leftbatY(videochip_7_leftbaty_2), .rightbatX(videochip_7_rightbatx_2), .chipID_2(chipID_2),
    .ballX_2(ballX_2), .ballY_2(ballY_2), .leftbatY_2(leftbatY_2), .rightbatX_2(rightbatX_2),
    .video_column(videocolumn_8));
endmodule

module videochip (
  input  [4:0] chipID,
  input  [4:0] ballX,
  input  [4:0] ballY,
  input  [4:0] leftbatY,
  input  [4:0] rightbatX,
  output [31:0] video_column,
  output [4:0] chipID_2,
  output [4:0] ballX_2,
  output [4:0] ballY_2,
  output [4:0] leftbatY_2,
  output [4:0] rightbatX_2
);

  wire comparator_1_eq, comparator_2_eq, comparator_3_eq, or_1_out;
  wire [4:0] multiplexer_1_out;
  wire [31:0] pull_resistor_1_node, pull_resistor_2_node, shifter_1_out, shifter_2_out;

  Comparator #(.width(5)) comparator_1 (.a(chipID), .b(ballX), .eq(comparator_1_eq));  // open: gt, lt
  Pull_Resistor pull_resistor_1 (.node(pull_resistor_1_node));
  Decoder #(.select(5)) decoder_1 (
    .out0(pull_resistor_1_node[0]), .out1(pull_resistor_1_node[1]), .out2(pull_resistor_1_node[2]),
    .out3(pull_resistor_1_node[3]), .out4(pull_resistor_1_node[4]), .out5(pull_resistor_1_node[5]),
    .out6(pull_resistor_1_node[6]), .out7(pull_resistor_1_node[7]), .out8(pull_resistor_1_node[8]),
    .out9(pull_resistor_1_node[9]), .out10(pull_resistor_1_node[10]), .out11(pull_resistor_1_node[11]),
    .out12(pull_resistor_1_node[12]), .out13(pull_resistor_1_node[13]), .out14(pull_resistor_1_node[14]),
    .out15(pull_resistor_1_node[15]), .out16(pull_resistor_1_node[16]), .out17(pull_resistor_1_node[17]),
    .out18(pull_resistor_1_node[18]), .out19(pull_resistor_1_node[19]), .out20(pull_resistor_1_node[20]),
    .out21(pull_resistor_1_node[21]), .out22(pull_resistor_1_node[22]), .out23(pull_resistor_1_node[23]),
    .out24(pull_resistor_1_node[24]), .out25(pull_resistor_1_node[25]), .out26(pull_resistor_1_node[26]),
    .out27(pull_resistor_1_node[27]), .out28(pull_resistor_1_node[28]), .out29(pull_resistor_1_node[29]),
    .out30(pull_resistor_1_node[30]), .out31(pull_resistor_1_node[31]), .sel(ballY), .en(comparator_1_eq));
  Comparator #(.width(5)) comparator_2 (.a(chipID), .b(5'b00011), .eq(comparator_2_eq));  // open: gt, lt
  Comparator #(.width(5)) comparator_3 (.a(chipID), .b(5'b11100), .eq(comparator_3_eq));  // open: gt, lt
  or or_1 (or_1_out, comparator_2_eq, comparator_3_eq);
  assign video_column = pull_resistor_1_node | pull_resistor_2_node | shifter_1_out | shifter_2_out;  // OR_Gate or_2, 32 bits wide
  Pull_Resistor pull_resistor_2 (.node(pull_resistor_2_node));
  Decoder #(.select(5)) decoder_2 (
    .out0(pull_resistor_2_node[0]), .out1(pull_resistor_2_node[1]), .out2(pull_resistor_2_node[2]),
    .out3(pull_resistor_2_node[3]), .out4(pull_resistor_2_node[4]), .out5(pull_resistor_2_node[5]),
    .out6(pull_resistor_2_node[6]), .out7(pull_resistor_2_node[7]), .out8(pull_resistor_2_node[8]),
    .out9(pull_resistor_2_node[9]), .out10(pull_resistor_2_node[10]), .out11(pull_resistor_2_node[11]),
    .out12(pull_resistor_2_node[12]), .out13(pull_resistor_2_node[13]), .out14(pull_resistor_2_node[14]),
    .out15(pull_resistor_2_node[15]), .out16(pull_resistor_2_node[16]), .out17(pull_resistor_2_node[17]),
    .out18(pull_resistor_2_node[18]), .out19(pull_resistor_2_node[19]), .out20(pull_resistor_2_node[20]),
    .out21(pull_resistor_2_node[21]), .out22(pull_resistor_2_node[22]), .out23(pull_resistor_2_node[23]),
    .out24(pull_resistor_2_node[24]), .out25(pull_resistor_2_node[25]), .out26(pull_resistor_2_node[26]),
    .out27(pull_resistor_2_node[27]), .out28(pull_resistor_2_node[28]), .out29(pull_resistor_2_node[29]),
    .out30(pull_resistor_2_node[30]), .out31(pull_resistor_2_node[31]), .sel(multiplexer_1_out), .en(or_1_out));
  Multiplexer #(.width(5)) multiplexer_1 (
    .in0(leftbatY), .in1(rightbatX), .out(multiplexer_1_out), .sel(comparator_3_eq));  // open: en
  Shifter #(.width(32)) shifter_1 (.in(pull_resistor_2_node), .\dist (5'b00001), .out(shifter_1_out));
  Shifter #(.width(32)) shifter_2 (.in(shifter_1_out), .\dist (5'b00001), .out(shifter_2_out));
  Adder #(.width(5)) adder_1 (.a(5'b00001), .b(chipID), .out(chipID_2));  // open: cin, cout

  assign ballX_2 = ballX;
  assign ballY_2 = ballY;
  assign leftbatY_2 = leftbatY;
  assign rightbatX_2 = rightbatX;

  // Other names for the same wires on the sheet: bX[4:0] = ballX; bY[4:0] = ballY; ID[4:0] = chipID;
  //   Lby[4:0] = leftbatY; Rby[4:0] = rightbatX
endmodule

module inrange (
  input  [4:0] Yball,
  input  [4:0] Ybat,
  output shareArow
);

  wire comparator_1_eq, comparator_2_eq, comparator_3_eq;
  wire [4:0] adder_1_out, adder_2_out;

  Adder #(.width(5)) adder_1 (.a(5'b00001), .b(Ybat), .out(adder_1_out));  // open: cin, cout
  Adder #(.width(5)) adder_2 (.a(5'b00010), .b(Ybat), .out(adder_2_out));  // open: cin, cout
  Comparator #(.width(5)) comparator_1 (.a(Yball), .b(Ybat), .eq(comparator_1_eq));  // open: gt, lt
  Comparator #(.width(5)) comparator_2 (.a(Yball), .b(adder_1_out), .eq(comparator_2_eq));  // open: gt, lt
  Comparator #(.width(5)) comparator_3 (.a(Yball), .b(adder_2_out), .eq(comparator_3_eq));  // open: gt, lt
  or or_1 (shareArow, comparator_1_eq, comparator_2_eq, comparator_3_eq);
endmodule

module reflect (
  input  [2:0] oldv,
  output [2:0] newv
);

  wire comparator_1_eq;
  wire [2:0] adder_1_out, not_1_out;

  // Probe on oldv
  assign not_1_out = ~oldv;  // NOT_Gate not_1, 3 bits wide
  Comparator #(.width(3)) comparator_1 (.a(3'b100), .b(oldv), .eq(comparator_1_eq));  // open: gt, lt
  Adder #(.width(3)) adder_1 (.a(not_1_out), .b(3'b001), .out(adder_1_out));  // open: cin, cout
  // Probe on newv
  Multiplexer #(.width(3)) multiplexer_1 (
    .in0(adder_1_out), .in1(not_1_out), .out(newv), .sel(comparator_1_eq));  // open: en
endmodule

module processor (
  input  reset,
  input  [7:0] ballX,
  input  [7:0] ballY,
  input  [7:0] Vxy,
  output [4:0] rightbatY
);

  wire cdm_8_mark5_1_data_inst, Cl, code, data, F2, F3, F4, F5, for_rbY_out, I_Osel, In_out_prime, mem,
       nand_1_out, not_1_out, not_2_out, RAM;
  wire [0:0] for_ballX_out;
  wire [1:0] or_1_out;
  wire [1:1] for_ballY_out, for_Vxy_out;
  wire [2:0] register_1_q;
  wire [3:0] I_Oadr;
  wire [7:0] cdm_8_mark5_1_data_out, cdm_8_mark5_1_pc, cdm_8_mark5_1_ps, cdm_8_mark5_1_r0, cdm_8_mark5_1_r1,
       cdm_8_mark5_1_r2, cdm_8_mark5_1_r3, cdm_8_mark5_1_sp, controlled_buffer_2_out, I_Odat;
  wire [7:4] cdm_8_mark5_1_addr;

  // Probe on cdm_8_mark5_1_r0
  // Probe on cdm_8_mark5_1_r2
  // Probe on cdm_8_mark5_1_r1
  and and_1 (I_Osel, not_1_out, Cl, data);
  // Probe on cdm_8_mark5_1_r3
  // Probe on cdm_8_mark5_1_pc
  Clock clock_1 (.out(Cl));
  not not_1 (not_1_out, nand_1_out);
  and and_2 (RAM, nand_1_out, data);
  // Probe on cdm_8_mark5_1_ps
  // Probe on cdm_8_mark5_1_sp
  CdM_8_mark5 cdm_8_mark5_1 (
    .clock(Cl), .addr({cdm_8_mark5_1_addr, I_Oadr}), .mem_read(In_out_prime), .mem_cycle(mem),
    .data_inst(cdm_8_mark5_1_data_inst), .data_out(cdm_8_mark5_1_data_out),
    .data_in(controlled_buffer_2_out), .r0(cdm_8_mark5_1_r0), .r1(cdm_8_mark5_1_r1), .r2(cdm_8_mark5_1_r2),
    .r3(cdm_8_mark5_1_r3), .PC(cdm_8_mark5_1_pc), .SP(cdm_8_mark5_1_sp), .PS(cdm_8_mark5_1_ps));  // open: IAck, IRQ, vec
  nand nand_1 (nand_1_out, cdm_8_mark5_1_addr[4], cdm_8_mark5_1_addr[5], cdm_8_mark5_1_addr[6], cdm_8_mark5_1_addr[7]);
  Decoder decoder_1 (.out0(code), .out1(data), .sel(cdm_8_mark5_1_data_inst), .en(mem));
  assign I_Odat = not_2_out ? cdm_8_mark5_1_data_out : 8'bz;  // Controlled_Buffer controlled_buffer_1
  not not_2 (not_2_out, In_out_prime);
  assign controlled_buffer_2_out = In_out_prime ? I_Odat : 8'bz;  // Controlled_Buffer controlled_buffer_2
  assign or_1_out = {2{for_Vxy_out[1]}} | {1'b0, for_ballX_out[0]} | {for_ballY_out[1], 1'b0};  // OR_Gate or_1, 2 bits wide
  and for_Vxy (for_Vxy_out[1], In_out_prime, F3, I_Osel);
  and for_ballX (for_ballX_out[0], In_out_prime, F4, I_Osel);
  and for_ballY (for_ballY_out[1], In_out_prime, F5, I_Osel);
  Decoder #(.select(4)) decoder_2 (
    .out2(F2), .out3(F3), .out4(F4), .out5(F5), .sel(I_Oadr));  // open: out0, out1, out6, out7, out8, out9, out10, out11, out12, out13, out14, out15, en
  Multiplexer #(.select(2), .width(8)) multiplexer_1 (
    .in1(ballX), .in2(ballY), .in3(Vxy), .out(I_Odat), .sel(or_1_out));  // open: in0, en
  Pull_Resistor pull_resistor_1 (.node(I_Oadr[0]));
  Pull_Resistor pull_resistor_2 (.node(I_Oadr[1]));
  Pull_Resistor pull_resistor_3 (.node(I_Oadr[2]));
  Pull_Resistor pull_resistor_4 (.node(I_Oadr[3]));
  Pull_Resistor pull_resistor_5 (.node(cdm_8_mark5_1_addr[4]));
  Pull_Resistor pull_resistor_6 (.node(cdm_8_mark5_1_addr[5]));
  Pull_Resistor pull_resistor_7 (.node(cdm_8_mark5_1_addr[6]));
  Pull_Resistor pull_resistor_8 (.node(cdm_8_mark5_1_addr[7]));
  Register register_1 (.D(I_Odat), .Q({rightbatY, register_1_q}), .clk(for_rbY_out));  // open: en, clr
  and for_rbY (for_rbY_out, ~In_out_prime, F2, I_Osel);  // AND_Gate
  ROM rom_1 (.addr({cdm_8_mark5_1_addr, I_Oadr}), .data(I_Odat), .sel(code));
  RAM ram_1 (.addr({cdm_8_mark5_1_addr, I_Oadr}), .data(I_Odat), .sel(RAM), .clk(Cl), .ld(In_out_prime), .clr(reset));

  // Other names for the same wires on the sheet: bX[7:0] = ballX; bY[7:0] = ballY; rd_wr_prime = In_out_prime
endmodule

module controller (
  input  [7:0] Vxy,
  input  [7:0] Xball,
  input  [7:0] Yball,
  input  [4:0] leftbatY,
  input  [4:0] rightbatY,
  input  Reset,
  input  Tact,
  output [4:0] out_8,
  output [4:0] Xball_2,
  output [4:0] Yball_2,
  output [4:0] leftbatY_2,
  output [4:0] out_12,
  output [7:0] scoreA,
  output [7:0] scoreB
);

  wire [7:0] undriven;

  Adder adder_1 (.a(Yball), .b(undriven));  // open: out, cin, cout

  assign out_8 = {5{1'b0}};
  assign out_12 = rightbatY;
  assign scoreA = {8{1'b0}};
  assign scoreB = {8{1'b0}};
  assign Vxy[6] = Vxy[7];
  // also tied to GND on the sheet: Vxy[7]

  // Other names for the same wires on the sheet: LeftBatX[4:0] = leftbatY_2; Vx[2:0] = Vxy[2:0]; Vy[2:0] = Vxy[5:3]

  // Notes on the sheet:
  //   to video subsystem
  //   location
  //   rightbatY
  //   to score
endmodule

module Kick_in_the_corner (
  input  [7:0] Vy,
  input  [7:0] Vy_2
);

  wire comparator_1_eq, comparator_2_eq, or_1_out;
  wire [7:0] adder_1_out, not_1_out;

  assign not_1_out = ~Vy_2;  // NOT_Gate not_1, 8 bits wide
  Comparator #(.mode("unsigned")) comparator_1 (.a(Vy_2), .b({8{1'b0}}), .eq(comparator_1_eq));  // open: gt, lt
  Comparator #(.mode("unsigned")) comparator_2 (.a({8{1'b1}}), .b(Vy_2), .eq(comparator_2_eq));  // open: gt, lt
  Adder adder_1 (.a(8'h1), .b(not_1_out), .out(adder_1_out));  // open: cin, cout
  or or_1 (or_1_out, comparator_1_eq, comparator_2_eq);
  Multiplexer #(.width(8)) multiplexer_1 (.in0(Vy_2), .in1(adder_1_out), .out(Vy), .sel(or_1_out));  // open: en
endmodule
