// Logisim project Tv-tennis.circ as structural Verilog: 7 circuits, main circuit main
module main (
);

  wire clock_1_out, R_out;
  wire [4:0] joystick_1_y, kinematic_controller_1_ballx, kinematic_controller_1_bally,
       kinematic_controller_1_leftyout, kinematic_controller_1_rightyout, kinematic_controller_1_zero,
       video_subsystem_1_ballx_2, video_subsystem_1_bally_2, video_subsystem_1_chipid_2,
       video_subsystem_1_leftbaty_2, video_subsystem_1_rightbatx_2, video_subsystem_2_ballx_2,
       video_subsystem_2_bally_2, video_subsystem_2_chipid_2, video_subsystem_2_leftbaty_2,
       video_subsystem_2_rightbatx_2, video_subsystem_3_ballx_2, video_subsystem_3_bally_2,
       video_subsystem_3_chipid_2, video_subsystem_3_leftbaty_2, video_subsystem_3_rightbatx_2;
  wire [7:0] kinematic_controller_1_scorea, kinematic_controller_1_scoreb;
  wire [31:0] video_subsystem_1_videocolumn, video_subsystem_1_videocolumn_2,
       video_subsystem_1_videocolumn_3, video_subsystem_1_videocolumn_4, video_subsystem_1_videocolumn_5,
       video_subsystem_1_videocolumn_6, video_subsystem_1_videocolumn_7, video_subsystem_1_videocolumn_8,
       video_subsystem_2_videocolumn, video_subsystem_2_videocolumn_2, video_subsystem_2_videocolumn_3,
       video_subsystem_2_videocolumn_4, video_subsystem_2_videocolumn_5, video_subsystem_2_videocolumn_6,
       video_subsystem_2_videocolumn_7, video_subsystem_2_videocolumn_8, video_subsystem_3_videocolumn,
       video_subsystem_3_videocolumn_2, video_subsystem_3_videocolumn_3, video_subsystem_3_videocolumn_4,
       video_subsystem_3_videocolumn_5, video_subsystem_3_videocolumn_6, video_subsystem_3_videocolumn_7,
       video_subsystem_3_videocolumn_8, video_subsystem_4_videocolumn, video_subsystem_4_videocolumn_2,
       video_subsystem_4_videocolumn_3, video_subsystem_4_videocolumn_4, video_subsystem_4_videocolumn_5,
       video_subsystem_4_videocolumn_6, video_subsystem_4_videocolumn_7, video_subsystem_4_videocolumn_8;

  Hex_Digit_Display hex_digit_display_1 ();  // open: value, dp
  Hex_Digit_Display hex_digit_display_2 ();  // open: value, dp
  Joystick #(.bits(5)) joystick_1 (.y(joystick_1_y));  // open: x
  Button R (.out(R_out));
  kinematic_controller kinematic_controller_1 (
    .zero(kinematic_controller_1_zero), .ballX(kinematic_controller_1_ballx),
    .ballY(kinematic_controller_1_bally), .rightYout(kinematic_controller_1_rightyout),
    .leftYout(kinematic_controller_1_leftyout), .reset(R_out), .leftYin(joystick_1_y),
    .scoreA(kinematic_controller_1_scorea), .tact(clock_1_out), .scoreB(kinematic_controller_1_scoreb));  // open: rightYin, xball, yball, vxy
  // Probe on kinematic_controller_1_scorea
  Clock clock_1 (.out(clock_1_out));
  DotMatrix #(.matrixcols(32), .matrixrows(32)) dotmatrix_1 (
    .col0(video_subsystem_1_videocolumn), .col1(video_subsystem_1_videocolumn_2),
    .col2(video_subsystem_1_videocolumn_3), .col3(video_subsystem_1_videocolumn_4),
    .col4(video_subsystem_1_videocolumn_5), .col5(video_subsystem_1_videocolumn_6),
    .col6(video_subsystem_1_videocolumn_7), .col7(video_subsystem_1_videocolumn_8),
    .col8(video_subsystem_2_videocolumn), .col9(video_subsystem_2_videocolumn_2),
    .col10(video_subsystem_2_videocolumn_3), .col11(video_subsystem_2_videocolumn_4),
    .col12(video_subsystem_2_videocolumn_5), .col13(video_subsystem_2_videocolumn_6),
    .col14(video_subsystem_2_videocolumn_7), .col15(video_subsystem_2_videocolumn_8),
    .col16(video_subsystem_3_videocolumn), .col17(video_subsystem_3_videocolumn_2),
    .col18(video_subsystem_3_videocolumn_3), .col19(video_subsystem_3_videocolumn_4),
    .col20(video_subsystem_3_videocolumn_5), .col21(video_subsystem_3_videocolumn_6),
    .col22(video_subsystem_3_videocolumn_7), .col23(video_subsystem_3_videocolumn_8),
    .col24(video_subsystem_4_videocolumn), .col25(video_subsystem_4_videocolumn_2),
    .col26(video_subsystem_4_videocolumn_3), .col27(video_subsystem_4_videocolumn_4),
    .col28(video_subsystem_4_videocolumn_5), .col29(video_subsystem_4_videocolumn_6),
    .col30(video_subsystem_4_videocolumn_7), .col31(video_subsystem_4_videocolumn_8));
  video_subsystem video_subsystem_1 (
    .chipID(kinematic_controller_1_zero), .ballX(kinematic_controller_1_ballx),
    .ballY(kinematic_controller_1_bally), .leftbatY(kinematic_controller_1_leftyout),
    .rightbatX(kinematic_controller_1_rightyout), .videocolumn(video_subsystem_1_videocolumn),
    .videocolumn_2(video_subsystem_1_videocolumn_2), .videocolumn_3(video_subsystem_1_videocolumn_3),
    .videocolumn_4(video_subsystem_1_videocolumn_4), .videocolumn_5(video_subsystem_1_videocolumn_5),
    .videocolumn_6(video_subsystem_1_videocolumn_6), .videocolumn_7(video_subsystem_1_videocolumn_7),
    .videocolumn_8(video_subsystem_1_videocolumn_8), .chipID_2(video_subsystem_1_chipid_2),
    .ballX_2(video_subsystem_1_ballx_2), .ballY_2(video_subsystem_1_bally_2),
    .leftbatY_2(video_subsystem_1_leftbaty_2), .rightbatX_2(video_subsystem_1_rightbatx_2));
  // Probe on kinematic_controller_1_scoreb
  video_subsystem video_subsystem_2 (
    .chipID(video_subsystem_1_chipid_2), .ballX(video_subsystem_1_ballx_2),
    .ballY(video_subsystem_1_bally_2), .leftbatY(video_subsystem_1_leftbaty_2),
    .rightbatX(video_subsystem_1_rightbatx_2), .videocolumn(video_subsystem_2_videocolumn),
    .videocolumn_2(video_subsystem_2_videocolumn_2), .videocolumn_3(video_subsystem_2_videocolumn_3),
    .videocolumn_4(video_subsystem_2_videocolumn_4), .videocolumn_5(video_subsystem_2_videocolumn_5),
    .videocolumn_6(video_subsystem_2_videocolumn_6), .videocolumn_7(video_subsystem_2_videocolumn_7),
    .videocolumn_8(video_subsystem_2_videocolumn_8), .chipID_2(video_subsystem_2_chipid_2),
    .ballX_2(video_subsystem_2_ballx_2), .ballY_2(video_subsystem_2_bally_2),
    .leftbatY_2(video_subsystem_2_leftbaty_2), .rightbatX_2(video_subsystem_2_rightbatx_2));
  video_subsystem video_subsystem_3 (
    .chipID(video_subsystem_2_chipid_2), .ballX(video_subsystem_2_ballx_2),
    .ballY(video_subsystem_2_bally_2), .leftbatY(video_subsystem_2_leftbaty_2),
    .rightbatX(video_subsystem_2_rightbatx_2), .videocolumn(video_subsystem_3_videocolumn),
    .videocolumn_2(video_subsystem_3_videocolumn_2), .videocolumn_3(video_subsystem_3_videocolumn_3),
    .videocolumn_4(video_subsystem_3_videocolumn_4), .videocolumn_5(video_subsystem_3_videocolumn_5),
    .videocolumn_6(video_subsystem_3_videocolumn_6), .videocolumn_7(video_subsystem_3_videocolumn_7),
    .videocolumn_8(video_subsystem_3_videocolumn_8), .chipID_2(video_subsystem_3_chipid_2),
    .ballX_2(video_subsystem_3_ballx_2), .ballY_2(video_subsystem_3_bally_2),
    .leftbatY_2(video_subsystem_3_leftbaty_2), .rightbatX_2(video_subsystem_3_rightbatx_2));
  video_subsystem video_subsystem_4 (
    .chipID(video_subsystem_3_chipid_2), .ballX(video_subsystem_3_ballx_2),
    .ballY(video_subsystem_3_bally_2), .leftbatY(video_subsystem_3_leftbaty_2),
    .rightbatX(video_subsystem_3_rightbatx_2), .videocolumn(video_subsystem_4_videocolumn),
    .videocolumn_2(video_subsystem_4_videocolumn_2), .videocolumn_3(video_subsystem_4_videocolumn_3),
    .videocolumn_4(video_subsystem_4_videocolumn_4), .videocolumn_5(video_subsystem_4_videocolumn_5),
    .videocolumn_6(video_subsystem_4_videocolumn_6), .videocolumn_7(video_subsystem_4_videocolumn_7),
    .videocolumn_8(video_subsystem_4_videocolumn_8));  // open: chipID_2, ballX_2, ballY_2, leftbatY_2, rightbatX_2
  Hex_Digit_Display hex_digit_display_3 ();  // open: value, dp
  Hex_Digit_Display hex_digit_display_4 ();  // open: value, dp
endmodule

module video_subsystem (
  input  [4:0] chipID,
  input  [4:0] ballX,
  input  [4:0] ballY,
  input  [4:0] leftbatY,
  input  [4:0] rightbatX,
  output [31:0] videocolumn,
  output [31:0] videocolumn_2,
  output [31:0] videocolumn_3,
  output [31:0] videocolumn_4,
  output [31:0] videocolumn_5,
  output [31:0] videocolumn_6,
  output [31:0] videocolumn_7,
  output [31:0] videocolumn_8,
  output [4:0] chipID_2,
  output [4:0] ballX_2,
  output [4:0] ballY_2,
  output [4:0] leftbatY_2,
  output [4:0] rightbatX_2
);

  wire [4:0] videochip_1_ballx_2, videochip_1_bally_2, videochip_1_chipid_2, videochip_1_leftbaty_2,
       videochip_1_rightbatx_2, videochip_2_ballx_2, videochip_2_bally_2, videochip_2_chipid_2,
       videochip_2_leftbaty_2, videochip_2_rightbatx_2, videochip_3_ballx_2, videochip_3_bally_2,
       videochip_3_chipid_2, videochip_3_leftbaty_2, videochip_3_rightbatx_2, videochip_4_ballx_2,
       videochip_4_bally_2, videochip_4_chipid_2, videochip_4_leftbaty_2, videochip_4_rightbatx_2,
       videochip_5_ballx_2, videochip_5_bally_2, videochip_5_chipid_2, videochip_5_leftbaty_2,
       videochip_5_rightbatx_2, videochip_6_ballx_2, videochip_6_bally_2, videochip_6_chipid_2,
       videochip_6_leftbaty_2, videochip_6_rightbatx_2, videochip_7_ballx_2, videochip_7_bally_2,
       videochip_7_chipid_2, videochip_7_leftbaty_2, videochip_7_rightbatx_2;

  videochip videochip_1 (
    .chipID(chipID), .ballX(ballX), .ballY(ballY), .leftbatY(leftbatY), .rightbatX(rightbatX),
    .chipID_2(videochip_1_chipid_2), .ballX_2(videochip_1_ballx_2), .ballY_2(videochip_1_bally_2),
    .leftbatY_2(videochip_1_leftbaty_2), .rightbatX_2(videochip_1_rightbatx_2), .video_column(videocolumn));
  videochip videochip_2 (
    .chipID(videochip_1_chipid_2), .ballX(videochip_1_ballx_2), .ballY(videochip_1_bally_2),
    .leftbatY(videochip_1_leftbaty_2), .rightbatX(videochip_1_rightbatx_2), .chipID_2(videochip_2_chipid_2),
    .ballX_2(videochip_2_ballx_2), .ballY_2(videochip_2_bally_2), .leftbatY_2(videochip_2_leftbaty_2),
    .rightbatX_2(videochip_2_rightbatx_2), .video_column(videocolumn_2));
  videochip videochip_3 (
    .chipID(videochip_2_chipid_2), .ballX(videochip_2_ballx_2), .ballY(videochip_2_bally_2),
    .leftbatY(videochip_2_leftbaty_2), .rightbatX(videochip_2_rightbatx_2), .chipID_2(videochip_3_chipid_2),
    .ballX_2(videochip_3_ballx_2), .ballY_2(videochip_3_bally_2), .leftbatY_2(videochip_3_leftbaty_2),
    .rightbatX_2(videochip_3_rightbatx_2), .video_column(videocolumn_3));
  videochip videochip_4 (
    .chipID(videochip_3_chipid_2), .ballX(videochip_3_ballx_2), .ballY(videochip_3_bally_2),
    .leftbatY(videochip_3_leftbaty_2), .rightbatX(videochip_3_rightbatx_2), .chipID_2(videochip_4_chipid_2),
    .ballX_2(videochip_4_ballx_2), .ballY_2(videochip_4_bally_2), .leftbatY_2(videochip_4_leftbaty_2),
    .rightbatX_2(videochip_4_rightbatx_2), .video_column(videocolumn_4));
  videochip videochip_5 (
    .chipID(videochip_4_chipid_2), .ballX(videochip_4_ballx_2), .ballY(videochip_4_bally_2),
    .leftbatY(videochip_4_leftbaty_2), .rightbatX(videochip_4_rightbatx_2), .chipID_2(videochip_5_chipid_2),
    .ballX_2(videochip_5_ballx_2), .ballY_2(videochip_5_bally_2), .leftbatY_2(videochip_5_leftbaty_2),
    .rightbatX_2(videochip_5_rightbatx_2), .video_column(videocolumn_5));
  videochip videochip_6 (
    .chipID(videochip_5_chipid_2), .ballX(videochip_5_ballx_2), .ballY(videochip_5_bally_2),
    .leftbatY(videochip_5_leftbaty_2), .rightbatX(videochip_5_rightbatx_2), .chipID_2(videochip_6_chipid_2),
    .ballX_2(videochip_6_ballx_2), .ballY_2(videochip_6_bally_2), .leftbatY_2(videochip_6_leftbaty_2),
    .rightbatX_2(videochip_6_rightbatx_2), .video_column(videocolumn_6));
  videochip videochip_7 (
    .chipID(videochip_6_chipid_2), .ballX(videochip_6_ballx_2), .ballY(videochip_6_bally_2),
    .leftbatY(videochip_6_leftbaty_2), .rightbatX(videochip_6_rightbatx_2), .chipID_2(videochip_7_chipid_2),
    .ballX_2(videochip_7_ballx_2), .ballY_2(videochip_7_bally_2), .leftbatY_2(videochip_7_leftbaty_2),
    .rightbatX_2(videochip_7_rightbatx_2), .video_column(videocolumn_7));
  videochip videochip_8 (
    .chipID(videochip_7_chipid_2), .ballX(videochip_7_ballx_2), .ballY(videochip_7_bally_2),
    .leftbatY(videochip_7_leftbaty_2), .rightbatX(videochip_7_rightbatx_2), .chipID_2(chipID_2),
    .ballX_2(ballX_2), .ballY_2(ballY_2), .leftbatY_2(leftbatY_2), .rightbatX_2(rightbatX_2),
    .video_column(videocolumn_8));
endmodule

module videochip (
  input  [4:0] chipID,
  input  [4:0] ballX,
  input  [4:0] ballY,
  input  [4:0] leftbatY,
  input  [4:0] rightbatX,
  output [31:0] video_column,
  output [4:0] chipID_2,
  output [4:0] ballX_2,
  output [4:0] ballY_2,
  output [4:0] leftbatY_2,
  output [4:0] rightbatX_2
);

  wire comparator_1_eq, comparator_2_eq, comparator_3_eq, or_1_out;
  wire [4:0] multiplexer_1_out;
  wire [31:0] decoder_1_out0, decoder_2_out0, shifter_1_out, shifter_2_out;

  Comparator #(.width(5)) comparator_1 (.a(chipID), .b(ballX), .eq(comparator_1_eq));  // open: gt, lt
  Decoder #(.select(5)) decoder_1 (
    .out0(decoder_1_out0[0]), .out1(decoder_1_out0[1]), .out2(decoder_1_out0[2]), .out3(decoder_1_out0[3]),
    .out4(decoder_1_out0[4]), .out5(decoder_1_out0[5]), .out6(decoder_1_out0[6]), .out7(decoder_1_out0[7]),
    .out8(decoder_1_out0[8]), .out9(decoder_1_out0[9]), .out10(decoder_1_out0[10]),
    .out11(decoder_1_out0[11]), .out12(decoder_1_out0[12]), .out13(decoder_1_out0[13]),
    .out14(decoder_1_out0[14]), .out15(decoder_1_out0[15]), .out16(decoder_1_out0[16]),
    .out17(decoder_1_out0[17]), .out18(decoder_1_out0[18]), .out19(decoder_1_out0[19]),
    .out20(decoder_1_out0[20]), .out21(decoder_1_out0[21]), .out22(decoder_1_out0[22]),
    .out23(decoder_1_out0[23]), .out24(decoder_1_out0[24]), .out25(decoder_1_out0[25]),
    .out26(decoder_1_out0[26]), .out27(decoder_1_out0[27]), .out28(decoder_1_out0[28]),
    .out29(decoder_1_out0[29]), .out30(decoder_1_out0[30]), .out31(decoder_1_out0[31]), .sel(ballY),
    .en(comparator_1_eq));
  Pull_Resistor pull_resistor_1 (.node(decoder_1_out0));
  Comparator #(.width(5)) comparator_2 (.a(chipID), .b(5'b00011), .eq(comparator_2_eq));  // open: gt, lt
  Comparator #(.width(5)) comparator_3 (.a(chipID), .b(5'b11100), .eq(comparator_3_eq));  // open: gt, lt
  Decoder #(.select(5)) decoder_2 (
    .out0(decoder_2_out0[0]), .out1(decoder_2_out0[1]), .out2(decoder_2_out0[2]), .out3(decoder_2_out0[3]),
    .out4(decoder_2_out0[4]), .out5(decoder_2_out0[5]), .out6(decoder_2_out0[6]), .out7(decoder_2_out0[7]),
    .out8(decoder_2_out0[8]), .out9(decoder_2_out0[9]), .out10(decoder_2_out0[10]),
    .out11(decoder_2_out0[11]), .out12(decoder_2_out0[12]), .out13(decoder_2_out0[13]),
    .out14(decoder_2_out0[14]), .out15(decoder_2_out0[15]), .out16(decoder_2_out0[16]),
    .out17(decoder_2_out0[17]), .out18(decoder_2_out0[18]), .out19(decoder_2_out0[19]),
    .out20(decoder_2_out0[20]), .out21(decoder_2_out0[21]), .out22(decoder_2_out0[22]),
    .out23(decoder_2_out0[23]), .out24(decoder_2_out0[24]), .out25(decoder_2_out0[25]),
    .out26(decoder_2_out0[26]), .out27(decoder_2_out0[27]), .out28(decoder_2_out0[28]),
    .out29(decoder_2_out0[29]), .out30(decoder_2_out0[30]), .out31(decoder_2_out0[31]),
    .sel(multiplexer_1_out), .en(or_1_out));
  or or_1 (or_1_out, comparator_2_eq, comparator_3_eq);
  Multiplexer #(.width(5)) multiplexer_1 (
    .in0(leftbatY), .in1(rightbatX), .out(multiplexer_1_out), .sel(comparator_3_eq));  // open: en
  assign video_column = decoder_1_out0 | decoder_2_out0 | shifter_1_out | shifter_2_out;  // OR_Gate or_2, 32 bits wide
  Pull_Resistor pull_resistor_2 (.node(decoder_2_out0));
  Shifter #(.width(32)) shifter_1 (.in(decoder_2_out0), .\dist (5'b00001), .out(shifter_1_out));
  Shifter #(.width(32)) shifter_2 (.in(shifter_1_out), .\dist (5'b00001), .out(shifter_2_out));
  Adder #(.width(5)) adder_1 (.a(5'b00001), .b(chipID), .out(chipID_2));  // open: cin, cout

  assign ballX_2 = ballX;
  assign ballY_2 = ballY;
  assign leftbatY_2 = leftbatY;
  assign rightbatX_2 = rightbatX;

  // Other names for the same wires on the sheet: bX[4:0] = ballX; bY[4:0] = ballY; ID[4:0] = chipID;
  //   Lby[4:0] = leftbatY; Rby[4:0] = rightbatX
endmodule

module kinematic_controller (
  input  reset,
  input  [4:0] leftYin,
  input  [4:0] rightYin,
  input  tact,
  output [4:0] zero,
  output [7:0] xball,
  output [4:0] ballX,
  output [4:0] ballY,
  output [7:0] yball,
  output [4:0] leftYout,
  output [7:0] vxy,
  output [4:0] rightYout,
  output [7:0] scoreA,
  output [7:0] scoreB
);

  wire adder_7_cout, adder_8_cout, adder_9_cout, adder_10_cout, adder_11_cout, adder_12_cout, and_1_out,
       and_2_out, and_3_out, and_4_out, and_5_out, and_6_out, and_7_out, and_8_out, Bcontact, hitA, hitB,
       inrange_1_sharearow, inrange_2_sharearow, LBcontact, or_1_out, or_2_out, or_3_out, or_4_out, or_5_out,
       or_6_out, RBcontact, xor_3_out, xor_4_out, xrefl, yrefl;
  wire [2:0] multiplexer_4_out, multiplexer_5_out, reflect_1_newv, reflect_2_newv;
  wire [4:0] multiplexer_1_out;
  wire [7:0] adder_1_out, adder_2_out, adder_3_out, adder_6_out, adder_7_out, adder_8_out, longVX, longVY,
       multiplexer_2_out, multiplexer_3_out, not_1_out, not_2_out;

  Adder adder_1 (.a({ballX, xball[2:0]}), .b(longVX), .out(adder_1_out));  // open: cin, cout
  Adder adder_2 (.a({ballY, yball[2:0]}), .b(longVY), .out(adder_2_out));  // open: cin, cout
  reflect reflect_1 (.oldv(vxy[2:0]), .newv(reflect_1_newv));
  reflect reflect_2 (.oldv(vxy[5:3]), .newv(reflect_2_newv));
  Register #(.width(5)) register_1 (.D(multiplexer_1_out), .Q(rightYout), .clk(and_1_out));  // open: en, clr
  Multiplexer #(.width(5)) multiplexer_1 (
    .in0(rightYin), .in1(5'b01111), .out(multiplexer_1_out), .sel(reset));  // open: en
  and and_1 (and_1_out, ~ballX[4], tact);  // AND_Gate
  Register x (.D(multiplexer_2_out), .Q({ballX, xball[2:0]}), .clk(and_2_out));  // open: en, clr
  Multiplexer #(.width(8)) multiplexer_2 (
    .in0(adder_1_out), .in1(8'hc0), .out(multiplexer_2_out), .sel(reset));  // open: en
  and and_2 (and_2_out, or_1_out, tact);
  or or_1 (or_1_out, reset, and_3_out);
  and and_3 (and_3_out, ~xrefl, ~Bcontact);  // AND_Gate
  Register y (.D(multiplexer_3_out), .Q({ballY, yball[2:0]}), .clk(and_7_out));  // open: en, clr
  Multiplexer #(.width(8)) multiplexer_3 (
    .in0(adder_2_out), .in1(8'h80), .out(multiplexer_3_out), .sel(reset));  // open: en
  or or_2 (or_2_out, reset, ~yrefl);  // OR_Gate
  Multiplexer #(.width(3)) multiplexer_4 (
    .in0(reflect_1_newv), .in1(3'b110), .out(multiplexer_4_out), .sel(reset));  // open: en
  Register #(.width(3)) Vx (.D(multiplexer_4_out), .Q(vxy[2:0]), .clk(and_4_out));  // open: en, clr
  and and_4 (and_4_out, or_3_out, tact);
  or or_3 (or_3_out, xrefl, Bcontact, reset);
  Register #(.width(3)) Vy (.D(multiplexer_5_out), .Q(vxy[5:3]), .clk(and_5_out));  // open: en, clr
  Multiplexer #(.width(3)) multiplexer_5 (
    .in0(reflect_2_newv), .in1(3'b001), .out(multiplexer_5_out), .sel(reset));  // open: en
  and and_5 (and_5_out, or_4_out, tact);
  or or_4 (or_4_out, yrefl, reset);
  Adder adder_3 (.a(scoreA), .b(8'h1), .out(adder_3_out));  // open: cin, cout
  Register register_2 (.D(adder_3_out), .Q(scoreA), .clk(and_6_out), .clr(reset));  // open: en
  and and_6 (and_6_out, hitA, tact);
  and and_7 (and_7_out, or_2_out, tact);
  assign not_1_out = ~{{6{vxy[2]}}, vxy[1:0]};  // NOT_Gate not_1, 8 bits wide
  Adder adder_4 (.a(not_1_out), .b(8'h1), .out(longVX));  // open: cin, cout
  assign not_2_out = ~{{6{vxy[5]}}, vxy[4:3]};  // NOT_Gate not_2, 8 bits wide
  Adder adder_5 (.a(not_2_out), .b(8'h1), .out(longVY));  // open: cin, cout
  Adder adder_6 (.a(scoreB), .b(8'h1), .out(adder_6_out));  // open: cin, cout
  and and_8 (and_8_out, hitB, tact);
  Adder adder_7 (.a({ballX, xball[2:0]}), .b(8'he4), .out(adder_7_out), .cout(adder_7_cout));  // open: cin
  Adder adder_8 (.a({ballX, xball[2:0]}), .b(8'h1c), .out(adder_8_out), .cout(adder_8_cout));  // open: cin
  Register register_3 (.D(adder_6_out), .Q(scoreB), .clk(and_8_out), .clr(reset));  // open: en
  Adder adder_9 (.a({ballX, xball[2:0]}), .b(longVX), .cout(adder_9_cout));  // open: out, cin
  Adder adder_10 (.a({ballY, yball[2:0]}), .b(longVY), .cout(adder_10_cout));  // open: out, cin
  and and_9 (hitA, xrefl, longVX[7]);
  and and_10 (hitB, xrefl, ~longVX[7]);  // AND_Gate
  Adder adder_11 (.a(adder_7_out), .b(longVX), .cout(adder_11_cout));  // open: out, cin
  Adder adder_12 (.a(adder_8_out), .b(longVX), .cout(adder_12_cout));  // open: out, cin
  xor xor_1 (xrefl, adder_9_cout, longVX[7]);
  xor xor_2 (yrefl, adder_10_cout, longVY[7]);
  or or_5 (or_5_out, adder_11_cout, adder_7_cout);
  xor xor_3 (xor_3_out, or_5_out, longVX[7]);
  inrange inrange_1 (.Yball(ballY), .Ybat(leftYin), .shareArow(inrange_1_sharearow));
  or or_6 (or_6_out, adder_12_cout, adder_8_cout);
  xor xor_4 (xor_4_out, or_6_out, longVX[7]);
  inrange inrange_2 (.Yball(ballY), .Ybat(rightYin), .shareArow(inrange_2_sharearow));
  and and_11 (LBcontact, xor_3_out, inrange_1_sharearow);
  and and_12 (RBcontact, xor_4_out, inrange_2_sharearow);
  or or_7 (Bcontact, LBcontact, RBcontact);
  assign leftYout = ~leftYin;  // NOT_Gate not_3, 5 bits wide

  assign vxy[7:6] = 2'b00;
  assign xball[7:3] = ballX;
  assign yball[7:3] = ballY;
  assign zero = {5{1'b0}};

  // Other names for the same wires on the sheet: vx[2:0] = vxy[2:0]; vy[2:0] = vxy[5:3]; lefttYin[4:0] = leftYin;
  //   vxneg = longVX[7]; vyneg = longVY[7]; rightYreg[4:0] = rightYout; xreg[7:0] = {ballX, xball[2:0]};
  //   yreg[7:0] = {ballY, yball[2:0]}
endmodule

module inrange (
  input  [4:0] Yball,
  input  [4:0] Ybat,
  output shareArow
);

  wire comparator_1_eq, comparator_2_eq, comparator_3_eq;
  wire [4:0] adder_1_out, adder_2_out;

  Adder #(.width(5)) adder_1 (.a(5'b00001), .b(Ybat), .out(adder_1_out));  // open: cin, cout
  Adder #(.width(5)) adder_2 (.a(5'b00010), .b(Ybat), .out(adder_2_out));  // open: cin, cout
  Comparator #(.width(5)) comparator_1 (.a(Yball), .b(Ybat), .eq(comparator_1_eq));  // open: gt, lt
  Comparator #(.width(5)) comparator_2 (.a(Yball), .b(adder_1_out), .eq(comparator_2_eq));  // open: gt, lt
  Comparator #(.width(5)) comparator_3 (.a(Yball), .b(adder_2_out), .eq(comparator_3_eq));  // open: gt, lt
  or or_1 (shareArow, comparator_1_eq, comparator_2_eq, comparator_3_eq);
endmodule

module reflect (
  input  [2:0] oldv,
  output [2:0] newv
);

  wire comparator_1_eq;
  wire [2:0] adder_1_out, not_1_out;

  // Probe on oldv
  assign not_1_out = ~oldv;  // NOT_Gate not_1, 3 bits wide
  Comparator #(.width(3)) comparator_1 (.a(3'b100), .b(oldv), .eq(comparator_1_eq));  // open: gt, lt
  Adder #(.width(3)) adder_1 (.a(not_1_out), .b(3'b001), .out(adder_1_out));  // open: cin, cout
  // Probe on newv
  Multiplexer #(.width(3)) multiplexer_1 (
    .in0(adder_1_out), .in1(not_1_out), .out(newv), .sel(comparator_1_eq));  // open: en
endmodule

module processor (
  input  reset,
  input  [7:0] ballX,
  input  [7:0] ballY,
  input  [7:0] Vxy,
  output [4:0] rightbatY
);

  wire cdm_8_mark5_1_data_inst, Cl, code, data, F2, F3, F4, F5, for_rbY_out, I_Osel, In_out_prime, mem,
       nand_1_out, not_1_out, not_2_out, RAM;
  wire [0:0] for_ballX_out;
  wire [1:0] or_1_out;
  wire [1:1] for_ballY_out, for_Vxy_out;
  wire [2:0] register_1_q;
  wire [3:0] I_Oadr;
  wire [7:0] cdm_8_mark5_1_data_out, cdm_8_mark5_1_pc, cdm_8_mark5_1_ps, cdm_8_mark5_1_r0, cdm_8_mark5_1_r1,
       cdm_8_mark5_1_r2, cdm_8_mark5_1_r3, cdm_8_mark5_1_sp, controlled_buffer_2_out, I_Odat;
  wire [7:4] cdm_8_mark5_1_addr;

  // Probe on cdm_8_mark5_1_r0
  // Probe on cdm_8_mark5_1_r2
  // Probe on cdm_8_mark5_1_r1
  and and_1 (I_Osel, not_1_out, Cl, data);
  // Probe on cdm_8_mark5_1_r3
  // Probe on cdm_8_mark5_1_pc
  Clock clock_1 (.out(Cl));
  not not_1 (not_1_out, nand_1_out);
  and and_2 (RAM, nand_1_out, data);
  // Probe on cdm_8_mark5_1_ps
  // Probe on cdm_8_mark5_1_sp
  CdM_8_mark5 cdm_8_mark5_1 (
    .clock(Cl), .addr({cdm_8_mark5_1_addr, I_Oadr}), .mem_read(In_out_prime), .mem_cycle(mem),
    .data_inst(cdm_8_mark5_1_data_inst), .data_out(cdm_8_mark5_1_data_out),
    .data_in(controlled_buffer_2_out), .r0(cdm_8_mark5_1_r0), .r1(cdm_8_mark5_1_r1), .r2(cdm_8_mark5_1_r2),
    .r3(cdm_8_mark5_1_r3), .PC(cdm_8_mark5_1_pc), .SP(cdm_8_mark5_1_sp), .PS(cdm_8_mark5_1_ps));  // open: IAck, IRQ, vec
  nand nand_1 (nand_1_out, cdm_8_mark5_1_addr[4], cdm_8_mark5_1_addr[5], cdm_8_mark5_1_addr[6], cdm_8_mark5_1_addr[7]);
  Decoder decoder_1 (.out0(code), .out1(data), .sel(cdm_8_mark5_1_data_inst), .en(mem));
  assign I_Odat = not_2_out ? cdm_8_mark5_1_data_out : 8'bz;  // Controlled_Buffer controlled_buffer_1
  not not_2 (not_2_out, In_out_prime);
  assign controlled_buffer_2_out = In_out_prime ? I_Odat : 8'bz;  // Controlled_Buffer controlled_buffer_2
  assign or_1_out = {2{for_Vxy_out[1]}} | {1'b0, for_ballX_out[0]} | {for_ballY_out[1], 1'b0};  // OR_Gate or_1, 2 bits wide
  and for_Vxy (for_Vxy_out[1], In_out_prime, F3, I_Osel);
  and for_ballX (for_ballX_out[0], In_out_prime, F4, I_Osel);
  and for_ballY (for_ballY_out[1], In_out_prime, F5, I_Osel);
  Decoder #(.select(4)) decoder_2 (
    .out2(F2), .out3(F3), .out4(F4), .out5(F5), .sel(I_Oadr));  // open: out0, out1, out6, out7, out8, out9, out10, out11, out12, out13, out14, out15, en
  Multiplexer #(.select(2), .width(8)) multiplexer_1 (
    .in1(ballX), .in2(ballY), .in3(Vxy), .out(I_Odat), .sel(or_1_out));  // open: in0, en
  Pull_Resistor pull_resistor_1 (.node(I_Oadr[0]));
  Pull_Resistor pull_resistor_2 (.node(I_Oadr[1]));
  Pull_Resistor pull_resistor_3 (.node(I_Oadr[2]));
  Pull_Resistor pull_resistor_4 (.node(I_Oadr[3]));
  Pull_Resistor pull_resistor_5 (.node(cdm_8_mark5_1_addr[4]));
  Pull_Resistor pull_resistor_6 (.node(cdm_8_mark5_1_addr[5]));
  Pull_Resistor pull_resistor_7 (.node(cdm_8_mark5_1_addr[6]));
  Pull_Resistor pull_resistor_8 (.node(cdm_8_mark5_1_addr[7]));
  Register register_1 (.D(I_Odat), .Q({rightbatY, register_1_q}), .clk(for_rbY_out));  // open: en, clr
  and for_rbY (for_rbY_out, ~In_out_prime, F2, I_Osel);  // AND_Gate
  ROM rom_1 (.addr({cdm_8_mark5_1_addr, I_Oadr}), .data(I_Odat), .sel(code));
  RAM ram_1 (.addr({cdm_8_mark5_1_addr, I_Oadr}), .data(I_Odat), .sel(RAM), .clk(Cl), .ld(In_out_prime), .clr(reset));

  // Other names for the same wires on the sheet: bX[7:0] = ballX; bY[7:0] = ballY; rd_wr_prime = In_out_prime
endmodule
